// Logisim project ALU.circ as structural Verilog: 1 circuit, main circuit ALU
module ALU (
  input  [31:0] A,
  input  [31:0] B,
  input  [4:0] Shift,
  input  [3:0] Codop,
  input  CarryIn,
  output [31:0] S,
  output [3:0] Flags
);

  wire N, Z;
  wire [31:0] ADC, ASR, BIC, bit_extender_1_out, CMN, CMP, EOR, ET, LSL, LSR, MUL, MVN, not_1_out, ORR, R,
       RSB, SBC, subtractor_1_out, subtractor_2_out, TST;

  assign bit_extender_1_out = {{31{CarryIn}}, CarryIn};  // Bit_Extender bit_extender_1
  assign not_1_out = ~A;  // NOT_Gate not_1, 32 bits wide
  assign ET = A & B;  // AND_Gate and_1, 32 bits wide
  assign EOR = A ^ B;  // XOR_Gate xor_1, 32 bits wide
  Shifter #(.width(32)) shifter_1 (.in(B), .\dist (Shift), .out(LSL));
  Shifter #(.shift("lr"), .width(32)) shifter_2 (.in(B), .\dist (Shift), .out(LSR));
  Shifter #(.shift("ar"), .width(32)) shifter_3 (.in(B), .\dist (Shift), .out(ASR));
  Adder #(.width(32)) adder_1 (.a(A), .b(B), .out(ADC), .cin(CarryIn));  // open: cout
  Subtractor #(.width(32)) subtractor_1 (.a(B), .b(A), .out(subtractor_1_out));  // open: bin, bout
  Subtractor #(.width(32)) subtractor_2 (.a(bit_extender_1_out), .b(32'h1), .out(subtractor_2_out));  // open: bin, bout
  Shifter #(.shift("rr"), .width(32)) shifter_4 (.in(B), .\dist (Shift), .out(R));
  assign TST = A & B;  // AND_Gate and_2, 32 bits wide
  Subtractor #(.width(32)) subtractor_3 (.a({32{1'b0}}), .b(A), .out(RSB));  // open: bin, bout
  Subtractor #(.width(32)) subtractor_4 (.a(B), .b(A), .out(CMP));  // open: bin, bout
  Adder #(.width(32)) adder_2 (.a(A), .b(B), .out(CMN));  // open: cin, cout
  assign ORR = A | B;  // OR_Gate or_1, 32 bits wide
  Multiplier #(.width(32)) multiplier_1 (.a(A), .b(B), .out(MUL));  // open: cin, cout
  assign BIC = B & not_1_out;  // AND_Gate and_3, 32 bits wide
  assign MVN = ~A;  // NOT_Gate not_2, 32 bits wide
  Adder #(.width(32)) adder_3 (.a(subtractor_1_out), .b(subtractor_2_out), .out(SBC));  // open: cin, cout
  Multiplexer #(.select(4), .width(32)) multiplexer_1 (
    .in0(ET), .in1(EOR), .in2(LSL), .in3(LSR), .in4(ASR), .in5(ADC), .in6(SBC), .in7(R), .in9(RSB),
    .in12(ORR), .in13(MUL), .in14(BIC), .in15(MVN), .out(S), .sel(Codop));  // open: in8, in10, in11, en
  Comparator #(.width(32)) comparator_1 (.b({32{1'b1}}));  // open: a, gt, eq, lt
  Comparator #(.width(32)) comparator_2 (.a(S), .b({32{1'b0}}), .eq(Z), .lt(N));  // open: gt

  // Other names for the same wires on the sheet: CIn = CarryIn; Co[3:0] = Codop; S_t[4:0] = Shift

  // Notes on the sheet:
  //   Note: for ROR, C = N
  //   Note 2: assume that shift > 0 for LSL and LSR
endmodule
